// Logisim project CU.circ as structural Verilog: 1 circuit, main circuit main
module main (
  input  [3:0] Data,
  input  [3:0] OP,
  output [3:0] Data_2,
  output [2:0] Reg,
  output Read,
  output Write,
  output [2:0] Rx,
  output [2:0] Ry,
  output [2:0] ALU_Sel
);
endmodule
