// Logisim project REGISTER.circ as structural Verilog: 3 circuits, main circuit main
module main (
  input  [3:0] Din,
  input  [2:0] R,
  input  Read,
  input  Write,
  input  [2:0] Rx,
  input  [2:0] Ry,
  input  [3:0] in_7,
  output [3:0] out_8,
  output [3:0] out_9
);

  wire undriven, undriven_2;
  wire [3:0] register_4_bits_1_out_4;

  RegFile regfile_1 (.RegNbr(R), .Sx(out_8), .Sy(out_9), .Write(Write), .Read(Read), .Din(Din), .Ry(Ry), .Rx(Rx));
  REGISTER_4_bits register_4_bits_1 (.CLK(undriven), .READ(undriven_2), .D(in_7), .out_4(register_4_bits_1_out_4));
endmodule

// REGISTER
module REGISTER_4_bits (
  input  [3:0] D,
  input  CLK,
  input  READ,
  output [3:0] out_4
);

  wire dlatch_1_s_b, dlatch_2_s_b, dlatch_3_s_b, dlatch_4_s_b;

  DLatch dlatch_1 (.D(D[3]), .CLK(CLK), .S_B(dlatch_1_s_b));  // open: S
  and and_1 (out_4[3], READ, dlatch_1_s_b);
  DLatch dlatch_2 (.D(D[2]), .CLK(CLK), .S_B(dlatch_2_s_b));  // open: S
  and and_2 (out_4[2], READ, dlatch_2_s_b);
  DLatch dlatch_3 (.D(D[1]), .CLK(CLK), .S_B(dlatch_3_s_b));  // open: S
  and and_3 (out_4[1], READ, dlatch_3_s_b);
  DLatch dlatch_4 (.D(D[0]), .CLK(CLK), .S_B(dlatch_4_s_b));  // open: S
  and and_4 (out_4[0], READ, dlatch_4_s_b);
endmodule

module RegFile (
  input  Write,
  input  Read,
  input  [3:0] Din,
  input  [2:0] RegNbr,
  input  [2:0] Ry,
  input  [2:0] Rx,
  output [3:0] Sx,
  output [3:0] Sy
);

  wire and_1_out, and_2_out, and_3_out, and_4_out, and_5_out, and_6_out, and_7_out, and_8_out, dec_3bit_1_p2,
       dec_3bit_1_p3, dec_3bit_1_p4, dec_3bit_1_p5, dec_3bit_1_p6, dec_3bit_1_p7, undriven, undriven_2;
  wire [3:0] register_4_bits_1_out_4, register_4_bits_2_out_4, register_4_bits_3_out_4,
       register_4_bits_4_out_4, register_4_bits_5_out_4, register_4_bits_6_out_4, register_4_bits_7_out_4,
       register_4_bits_8_out_4;

  // DEC_3Bit dec_3bit_1: pin names not known; wires that end beside it: RegNbr, dec_3bit_1_p2, dec_3bit_1_p3, dec_3bit_1_p4, dec_3bit_1_p5, dec_3bit_1_p6, dec_3bit_1_p7
  and and_1 (and_1_out, Write, dec_3bit_1_p2);
  and and_2 (and_2_out, Write, dec_3bit_1_p3);
  and and_3 (and_3_out, Write, dec_3bit_1_p4);
  and and_4 (and_4_out, Write, dec_3bit_1_p5);
  and and_5 (and_5_out, Write, dec_3bit_1_p6);
  and and_6 (and_6_out, Write, dec_3bit_1_p7);
  and and_7 (and_7_out, Write, undriven);
  and and_8 (and_8_out, undriven_2, Write);
  REGISTER_4_bits register_4_bits_1 (.CLK(and_1_out), .READ(Read), .D(Din), .out_4(register_4_bits_1_out_4));
  REGISTER_4_bits register_4_bits_2 (.CLK(and_2_out), .READ(Read), .D(Din), .out_4(register_4_bits_2_out_4));
  REGISTER_4_bits register_4_bits_3 (.CLK(and_3_out), .READ(Read), .D(Din), .out_4(register_4_bits_3_out_4));
  REGISTER_4_bits register_4_bits_4 (.CLK(and_4_out), .READ(Read), .D(Din), .out_4(register_4_bits_4_out_4));
  REGISTER_4_bits register_4_bits_5 (.CLK(and_5_out), .READ(Read), .D(Din), .out_4(register_4_bits_5_out_4));
  REGISTER_4_bits register_4_bits_6 (.CLK(and_6_out), .READ(Read), .D(Din), .out_4(register_4_bits_6_out_4));
  REGISTER_4_bits register_4_bits_7 (.CLK(and_7_out), .READ(Read), .D(Din), .out_4(register_4_bits_7_out_4));
  REGISTER_4_bits register_4_bits_8 (.CLK(and_8_out), .READ(Read), .D(Din), .out_4(register_4_bits_8_out_4));
  // MUX_8__1_4_Bit mux_8_1_4_bit_1: pin names not known; wires that end beside it: register_4_bits_1_out_4, register_4_bits_2_out_4, register_4_bits_3_out_4, register_4_bits_4_out_4, register_4_bits_5_out_4, register_4_bits_6_out_4, register_4_bits_7_out_4, register_4_bits_8_out_4, Rx, Sx
  // MUX_8__1_4_Bit mux_8_1_4_bit_2: pin names not known; wires that end beside it: register_4_bits_1_out_4, register_4_bits_2_out_4, register_4_bits_3_out_4, register_4_bits_4_out_4, register_4_bits_5_out_4, register_4_bits_6_out_4, register_4_bits_7_out_4, register_4_bits_8_out_4, Ry, Sy
endmodule
