// Logisim project lib.circ as structural Verilog
module HALF_ADDER (
  input  A,
  input  B,
  output S,
  output out_4
);

  and and_1 (out_4, A, B);
  xor xor_1 (S, A, B);
endmodule

module MUX_2__1 (
  input  A,
  input  B,
  input  SEL,
  output S
);

  wire and_1_out, and_2_out, not_1_out;

  not not_1 (not_1_out, SEL);
  buf and_1 (and_1_out, B);  // AND_Gate
  and and_2 (and_2_out, A, not_1_out);
  or or_1 (S, and_1_out, and_2_out);
endmodule

module FULL_ADDER_1_Bit (
  input  A,
  input  B,
  input  C_i,
  output S,
  output C_o
);

  wire and_1_out, and_2_out, xor_1_out;

  xor xor_1 (xor_1_out, A, B);
  and and_1 (and_1_out, A, B);
  and and_2 (and_2_out, xor_1_out, C_i);
  xor xor_2 (S, xor_1_out, C_i);
  or or_1 (C_o, and_1_out, and_2_out);
endmodule

module DEC_3Bit (
  input  [2:0] in_1,
  output S0,
  output S1,
  output S2,
  output S3,
  output S4,
  output S5,
  output S6,
  output S7
);

  wire not_1_out, not_2_out, not_3_out, not_4_out, not_5_out, not_6_out, not_7_out, not_8_out, not_9_out,
       not_10_out, not_11_out, not_12_out;

  not not_1 (not_1_out, in_1[0]);
  not not_2 (not_2_out, in_1[1]);
  not not_3 (not_3_out, in_1[2]);
  not not_4 (not_4_out, in_1[1]);
  not not_5 (not_5_out, in_1[2]);
  not not_6 (not_6_out, in_1[0]);
  not not_7 (not_7_out, in_1[2]);
  not not_8 (not_8_out, in_1[2]);
  not not_9 (not_9_out, in_1[0]);
  not not_10 (not_10_out, in_1[1]);
  not not_11 (not_11_out, in_1[1]);
  not not_12 (not_12_out, in_1[0]);
  nand nand_1 (S0, not_1_out, not_2_out, not_3_out);
  nand nand_2 (S1, in_1[0], not_4_out, not_5_out);
  nand nand_3 (S2, not_6_out, in_1[1], not_7_out);
  nand nand_4 (S3, in_1[0], in_1[1], not_8_out);
  nand nand_5 (S4, not_9_out, not_10_out, in_1[2]);
  nand nand_6 (S5, in_1[0], not_11_out, in_1[2]);
  nand nand_7 (S6, not_12_out, in_1[1], in_1[2]);
  nand nand_8 (S7, in_1[0], in_1[1], in_1[2]);
endmodule

// MUX
module MUX_8__1_1Bit (
  input  in_1,
  input  in_2,
  input  in_3,
  input  in_4,
  input  in_5,
  input  in_6,
  input  in_7,
  input  in_8,
  input  [2:0] in_9,
  output out_10
);

  wire and_1_out, and_2_out, and_3_out, and_4_out, and_5_out, and_6_out, and_7_out, and_8_out, not_1_out,
       not_2_out, not_3_out;

  not not_1 (not_1_out, in_9[1]);
  not not_2 (not_2_out, in_9[2]);
  not not_3 (not_3_out, in_9[0]);
  and and_1 (and_1_out, in_1, not_2_out, not_1_out, not_3_out);
  and and_2 (and_2_out, in_2, not_2_out, not_1_out, in_9[0]);
  and and_3 (and_3_out, in_3, not_2_out, in_9[1], not_3_out);
  and and_4 (and_4_out, in_4, not_2_out, in_9[1], in_9[0]);
  and and_5 (and_5_out, in_5, in_9[2], not_1_out, not_3_out);
  and and_6 (and_6_out, in_6, in_9[2], not_1_out, in_9[0]);
  and and_7 (and_7_out, in_7, in_9[2], in_9[1], not_3_out);
  and and_8 (and_8_out, in_8, in_9[2], in_9[1], in_9[0]);
  or or_1 (out_10, and_1_out, and_2_out, and_3_out, and_4_out, and_5_out, and_6_out, and_7_out, and_8_out);
endmodule

module FLIP_FLOP_D (
  input  D,
  input  CLK,
  output S
);

  wire and_1_out, and_2_out, nor_1_out, not_1_out;

  not not_1 (not_1_out, D);
  and and_1 (and_1_out, D, CLK);
  and and_2 (and_2_out, not_1_out, CLK);
  nor nor_1 (nor_1_out, and_1_out, S);
  nor nor_2 (S, nor_1_out, and_2_out);
endmodule

module MAJ (
  input  a,
  input  b,
  input  c,
  output out_4
);

  wire and_1_out, and_2_out, and_3_out, and_4_out, not_1_out, not_2_out, not_3_out;

  not not_1 (not_1_out, a);
  not not_2 (not_2_out, b);
  not not_3 (not_3_out, c);
  and and_1 (and_1_out, not_1_out, b, c);
  and and_2 (and_2_out, a, not_2_out, c);
  and and_3 (and_3_out, a, b, not_3_out);
  and and_4 (and_4_out, c, b, a);
  or or_1 (out_4, and_1_out, and_2_out, and_3_out, and_4_out);
endmodule
